# Fritzing sketch PedalBoi_Schematic (saved by Fritzing 0.9.4)
breadboards: 3

parts:
  Seed = Daisy Seed [chip_label=IC package="DIP (Dual Inline) [THT]"]
  Output_Jack = 1/4 inch mono jack [part_number=2223-SJ-63062B package=audio-jack-6.5mm-panel-mount]
  Input_Jack = 1/4 inch mono jack [part_number=2223-SJ-63062B package=audio-jack-6.5mm-panel-mount]
  Input_R1 = Resistor [tolerance=±5% resistance=2M package="0805 [SMD]"]
  Input_C1 = Electrolytic Capacitor [capacitance=10µF package="0405 [SMD, electrolytic]"]
  Input_R3 = Resistor [tolerance=±5% resistance=100k package="0805 [SMD]"]
  Input_R2 = Resistor [tolerance=±5% resistance=100k package="0805 [SMD]"]
  Input_Bias_R = Resistor [tolerance=±5% resistance=2M package="0805 [SMD]"]
  Input_C2 = Electrolytic Capacitor [capacitance=1µF package="0405 [SMD, electrolytic]"]
  Ouput_C1 = Electrolytic Capacitor [capacitance=10µF package="0405 [SMD, electrolytic]"]
  Output_R4 = Resistor [tolerance=±5% resistance=2M package="0805 [SMD]"]
  Output_C4 = Electrolytic Capacitor [capacitance=10µF package="0405 [SMD, electrolytic]"]
  Output_R1 = Resistor [tolerance=±5% resistance=2M package="0805 [SMD]"]
  Ouput_Buffer = Dual Op-Amp [part_number=NJM4580D package=dip08]
  Input_Buffer/Audio_Bias = Dual Op-Amp [part_number=MCP6002 package=dip08]
  Ouput_R2 = Resistor [tolerance=±5% resistance=2M package="0805 [SMD]"]
  DC_Input = DC Power [voltage=15]
  Input_C3 = Ceramic Capacitor [capacitance=100nF package="100 mil [THT, multilayer]"]
  Input_C4 = Ceramic Capacitor [capacitance=100nF package="100 mil [THT, multilayer]"]
  Output_R3 = Resistor [tolerance=±5% resistance=110 package="1206 [SMD]"]
  Current_Protection = Diode [package=diode-hv]
  Output_C2 = Ceramic Capacitor [capacitance=100nF package="100 mil [THT, multilayer]"]
  Output_C3 = Ceramic Capacitor [capacitance=100nF package="100 mil [THT, multilayer]"]
  Foot_Switch = NKK M2032SS1W01 3PDT Toggle Switch [part_number=EG5491 package=THT]
  LED_R = Resistor [tolerance=±5% resistance=100k package="0805 [SMD]"]
  LED = smd LED [color="Red (633nm)" package="0805 [SMD]"]

nets:
  N1: Seed.pin_16, Input_C2.-
  N2: Seed.pin_18, Ouput_C1.+
  GND: Seed.pin_20, Seed.pin_40, Output_Jack.Sleeve, Input_Jack.Sleeve, Input_R1.Pin_1, Input_R3.Pin_1, Output_R4.Pin_1, Output_R1.Pin_1, Ouput_Buffer.A_V-, Input_Buffer/Audio_Bias.A_V+, DC_Input.V-, Input_C3.1, Input_C4.1, Output_C2.0, Output_C3.0, LED.cathode
  N3: Seed.pin_38, Input_Buffer/Audio_Bias.A_V-, Input_C3.0, Input_C4.0
  N4: Output_Jack.Tip, Foot_Switch.C2
  N5: Input_Jack.Tip, Foot_Switch.C3
  N6: Input_R1.Pin_0, Input_C1.+, Foot_Switch.L3-1
  N7: Input_C1.-, Input_Bias_R.Pin_1, Input_Buffer/Audio_Bias.B_+IN
  N8: Input_R3.Pin_0, Input_R2.Pin_0, Ouput_Buffer.A_V+, Ouput_R2.Pin_0, Current_Protection.C, Foot_Switch.C1
  N9: Input_R2.Pin_1, Input_Buffer/Audio_Bias.A_+IN
  N10: Input_Bias_R.Pin_0, Input_Buffer/Audio_Bias.A_OUT, Input_Buffer/Audio_Bias.A_-IN
  N11: Input_C2.+, Input_Buffer/Audio_Bias.B_-IN, Input_Buffer/Audio_Bias.B_OUT
  N12: Ouput_C1.-, Output_R1.Pin_0, Ouput_Buffer.A_+IN, Ouput_R2.Pin_1, Output_C2.1, Output_C3.1
  N13: Output_R4.Pin_0, Output_C4.+, Output_R3.Pin_0
  N14: Output_C4.-, Foot_Switch.L2-1
  N15: Ouput_Buffer.A_OUT, Ouput_Buffer.A_-IN, Output_R3.Pin_1
  N16: DC_Input.V+, Current_Protection.A
  N17: Foot_Switch.L1-1, LED_R.Pin_0
  N18: Foot_Switch.L2-2, Foot_Switch.L3-2
  N19: LED_R.Pin_1, LED.anode

custom parts:
  Daisy Seed: Daisy is an embedded platform for music. It features everything you need for creating high fidelity audio hardware devices. Just plug in a USB cable and start making sound! No soldering required.
  1/4 inch mono jack: 1/4 inch mono Audio Jack Simple 1/4 inch panel mount audio jack.
  NKK M2032SS1W01 3PDT Toggle Switch: NKK M2032SS1W01 3PDT Toggle Switch This switch has three poles and two position
